# Fritzing sketch nodemcu-wifibot (saved by Fritzing 0.9.4)
breadboards: 2

parts:
  U1 = ESP8266 NodeMCU LoLin module
  SN754410_or_L293 = H-Bridge [package=THT]
  6V_battery_(4_x_AAA) = 4 x AAA Battery Mount
  power_switch = Toggle Switch [package=THT]
  part = DC Motor [part_number="RIGHT motor"]
  LEFT_motor = DC Motor
  R1 = Resistor [tolerance=±1% resistance=100k package="2512 [SMD]"]
  R2 = Resistor [tolerance=±1% resistance=100k package="2512 [SMD]"]
  Q1 = NPN-Transistor [part_number="Small NPN transistor (i.e. BC547)" package="TO92 [THT]"]
  R3 = Resistor [tolerance=±1% resistance=1k package="2512 [SMD]"]
  LED1 = LED - 5mm [color="Red (633nm)" package="5 mm [THT]"]
  LED2 = LED - 5mm [color="Red (633nm)" package="5 mm [THT]"]
  R4 = Resistor [tolerance=±1% resistance=220 package="2512 [SMD]"]

nets:
  N1: U1.D0, R3.Pin_0
  N2: U1.D1, SN754410_or_L293.1A
  N3: U1.D2, SN754410_or_L293.2A
  N4: U1.D4, SN754410_or_L293.1_2EN
  GND: U1.GND, SN754410_or_L293.GND1, SN754410_or_L293.GND2, SN754410_or_L293.GND3, SN754410_or_L293.GND4, 6V_battery_(4_x_AAA).-, R2.Pin_1, Q1.E
  N5: U1.D5, SN754410_or_L293.4A
  N6: U1.D6, SN754410_or_L293.3A
  N7: U1.D7, SN754410_or_L293.3_4EN
  N8: U1.Vin, SN754410_or_L293.VCC2, SN754410_or_L293.VCC1, power_switch.L1, R1.Pin_0, R4.Pin_1
  N9: U1.A0, R1.Pin_1, R2.Pin_0
  N10: SN754410_or_L293.1Y, LEFT_motor.pin_2
  N11: SN754410_or_L293.2Y, LEFT_motor.pin_1
  N12: SN754410_or_L293.3Y, part.pin_2
  N13: SN754410_or_L293.4Y, part.pin_1
  N14: 6V_battery_(4_x_AAA).+, power_switch.COM
  N15: Q1.B, R3.Pin_1
  N16: Q1.C, LED1.cathode
  N17: LED1.anode, LED2.cathode
  N18: LED2.anode, R4.Pin_0

custom parts:
  ESP8266 NodeMCU LoLin module: ESP8266 based NodeMCU
